# Fritzing sketch AtariPunkConsoleBreadboard (saved by Fritzing 0.9.3b)
breadboards: 1

parts:
  IC1 = IC, DIP package, 8 pins [chip_label=IC]
  IC2 = IC, DIP package, 8 pins [chip_label=IC]
  C1 = Ceramic Capacitor [capacitance="100 nF" package="0805 [SMD, multilayer]"]
  R1 = Resistor [tolerance=±5% resistance=220 package="2010 [SMD]"]
  R2 = Rotary Potentiometer (Small) [maximum_resistance=100kΩ package=THT]
  C2 = Electrolytic Capacitor [capacitance=1μF package="0405 [SMD, electrolytic]"]
  C3 = Ceramic Capacitor [capacitance="100 nF" package="0805 [SMD, multilayer]"]
  R3 = Rotary Potentiometer (Small) [maximum_resistance=100kΩ package=THT]
  R4 = Resistor [tolerance=±5% resistance=220 package="2010 [SMD]"]
  R5 = Resistor [tolerance=±5% resistance=220 package="2010 [SMD]"]
  SP1 = SPEAKER [package=pcb_mount_speaker]
  VCC1 = Battery block 9V

nets:
  N1: IC1.pin1, IC2.pin1, C1.0, C3.1, R5.Pin_1, SP1.+, VCC1.-
  N2: IC1.pin2, IC1.pin6, C1.1, R1.Pin_1
  N3: IC1.pin3, IC2.pin2
  N4: IC1.pin4, IC1.pin8, IC2.pin4, IC2.pin8, R2.wiper, R3.wiper, VCC1.+
  N5: IC1.pin7, R1.Pin_0, R2.leg2
  N6: IC2.pin3, C2.-
  N7: IC2.pin6, IC2.pin7, C3.0, R3.leg2
  N8: C2.+, R4.Pin_0
  N9: R4.Pin_1, R5.Pin_0, SP1.-
