# Fritzing sketch LM555OscBreadboard (saved by Fritzing 0.9.3b)
breadboards: 1

parts:
  IC1 = IC, DIP package, 8 pins [chip_label=IC]
  C1 = Ceramic Capacitor [capacitance="100 nF" package="0805 [SMD, multilayer]"]
  R1 = Resistor [tolerance=±5% resistance=220 package="2010 [SMD]"]
  R2 = Rotary Potentiometer (Small) [maximum_resistance=100kΩ package=THT]
  SP1 = SPEAKER [package=pcb_mount_speaker]
  VCC1 = Battery block 9V
  C2 = Electrolytic Capacitor [capacitance=100μF package="0807 [SMD, electrolytic]"]
  R3 = Resistor [tolerance=±5% resistance=220 package="2010 [SMD]"]
  R4 = Resistor [tolerance=±5% resistance=220 package="2010 [SMD]"]

nets:
  N1: IC1.pin1, C1.0, SP1.+, VCC1.-, R4.Pin_1
  N2: IC1.pin2, IC1.pin6, C1.1, R1.Pin_1
  N3: IC1.pin3, C2.+
  N4: IC1.pin4, IC1.pin8, R2.wiper, VCC1.+
  N5: IC1.pin7, R1.Pin_0, R2.leg2
  N6: SP1.-, R3.Pin_1, R4.Pin_0
  N7: C2.-, R3.Pin_0
